# Fritzing sketch hethongnhung (saved by Fritzing 0.9.3b)
breadboards: 1

parts:
  Part1 = Arduino Leonardo (Rev3b)
  Mod1 = KY-026 Flame Sensor Module [package="Breakout board"]
  Part2 = LCD1602-I2C
  Keypad4x1 = Keypad Membran 4x4
  U1 = GAS_SENSOR [package=mq-3]
  J1 = Piezo Speaker
  LED1 = smd LED [color="Red (633nm)" package="0805 [SMD]"]

nets:
  N1: Part1.D2/SDA, LED1.cathode
  N2: Part1.D3_PWM/SCL, Keypad4x1.Pin8
  N3: Part1.D4/A6, Keypad4x1.Pin7
  N4: Part1.D5_PWM, Keypad4x1.Pin6
  N5: Part1.D6_PWM/A7, Keypad4x1.Pin5
  N6: Part1.D7, Keypad4x1.Pin4
  5V: Part1.5V, Mod1.+, Part2.VCC, U1.B1
  GND: Part1.GND, Mod1.G, Part2.GND, U1.A1, J1.pin1, LED1.anode
  N7: Part1.A1, Mod1.A0
  N8: Part1.A4, Part2.SDA
  N9: Part1.A5, Part2.SCL
  N10: Part1.D8/A8, Keypad4x1.Pin3
  N11: Part1.D9_PWM/A9, Keypad4x1.Pin2
  N12: Part1.D10_PWM/A10, Keypad4x1.Pin1
  N13: Part1.D13_PWM, J1.pin2

custom parts:
  KY-026 Flame Sensor Module: KY-026 Flame Sensor Module reacts in the presence of fire.
  LCD1602-I2C: A standard character display, usually with 2x16 characters. Comes in many colors with LCM1602 IIC attached.
  Keypad Membran 4x4: Membrane Keypad 4x4 Matrix
